// Logisim project 4-Bit-Microprocessor.circ as structural Verilog: 12 circuits, main circuit main
module main (
  input  [15:0] Control_Word,
  input  CLK,
  input  [3:0] constIn,
  input  [3:0] Data_In,
  output [3:0] Address_Out,
  output [3:0] Data_Out,
  output [2:0] PZN
);

  wire [3:0] function_unit_1_f, multiplexer_2_out, regfile_1_b__out;

  RegFile regfile_1 (
    .D_In(multiplexer_2_out), .Write(Control_Word[0]), .D_Address(Control_Word[3:1]), .A_Out(Address_Out),
    .A_Address(Control_Word[15:13]), .B__Out(regfile_1_b__out), .B_Address(Control_Word[11:9]), .CLK(CLK));
  Multiplexer #(.width(4), .enable("false")) multiplexer_1 (
    .in0(regfile_1_b__out), .in1(constIn), .out(Data_Out), .sel(Control_Word[12]));
  Function_Unit function_unit_1 (
    .B_Out(Data_Out), .A_Out(Address_Out), .Function_Select(Control_Word[7:4]), .PZN(PZN),
    .F(function_unit_1_f));
  Multiplexer #(.width(4), .enable("false")) multiplexer_2 (
    .in0(function_unit_1_f), .in1(Data_In), .out(multiplexer_2_out), .sel(Control_Word[8]));

  // Notes on the sheet:
  //   MuxB[12]
  //   MuxF[8]
  //   D Address[3:1]
  //   RegfileWrite[0]
  //   A Address[15:13]
  //   B Address[11:9]
  //   Function Select[7:4]
endmodule

module RegFile (
  input  [3:0] D_In,
  input  Write,
  input  [2:0] A_Address,
  input  [2:0] D_Address,
  input  [2:0] B_Address,
  input  CLK,
  output [3:0] A_Out,
  output [3:0] B__Out
);

  wire and_1_out, and_2_out, and_3_out, and_4_out, and_5_out, and_6_out, and_7_out, and_8_out,
       decoder_1_out0, decoder_1_out1, decoder_1_out2, decoder_1_out3, decoder_1_out4, decoder_1_out5,
       decoder_1_out6, decoder_1_out7;
  wire [3:0] R0_q, R1_q, R2_q, R3_q, R4_q, R5_q, R6_q, R7_q;

  Decoder #(.select(3), .enable("false")) decoder_1 (
    .out0(decoder_1_out0), .out1(decoder_1_out1), .out2(decoder_1_out2), .out3(decoder_1_out3),
    .out4(decoder_1_out4), .out5(decoder_1_out5), .out6(decoder_1_out6), .out7(decoder_1_out7),
    .sel(D_Address));
  Register #(.width(4)) R0 (.D(D_In), .en(and_1_out), .Q(R0_q), .clk(CLK));  // open: clr
  and and_1 (and_1_out, Write, decoder_1_out0);
  Register #(.width(4)) R1 (.D(D_In), .en(and_2_out), .Q(R1_q), .clk(CLK));  // open: clr
  and and_2 (and_2_out, decoder_1_out1, Write);
  and and_3 (and_3_out, Write, decoder_1_out2);
  and and_4 (and_4_out, decoder_1_out3, Write);
  and and_5 (and_5_out, Write, decoder_1_out4);
  and and_6 (and_6_out, decoder_1_out5, Write);
  and and_7 (and_7_out, Write, decoder_1_out6);
  and and_8 (and_8_out, decoder_1_out7, Write);
  Register #(.width(4)) R2 (.D(D_In), .en(and_3_out), .Q(R2_q), .clk(CLK));  // open: clr
  Register #(.width(4)) R3 (.D(D_In), .en(and_4_out), .Q(R3_q), .clk(CLK));  // open: clr
  Register #(.width(4)) R4 (.D(D_In), .en(and_5_out), .Q(R4_q), .clk(CLK));  // open: clr
  Register #(.width(4)) R5 (.D(D_In), .en(and_6_out), .Q(R5_q), .clk(CLK));  // open: clr
  Register #(.width(4)) R6 (.D(D_In), .en(and_7_out), .Q(R6_q), .clk(CLK));  // open: clr
  Register #(.width(4)) R7 (.D(D_In), .en(and_8_out), .Q(R7_q), .clk(CLK));  // open: clr
  Multiplexer #(.select(3), .width(4), .enable("false")) multiplexer_1 (
    .in0(R0_q), .in1(R1_q), .in2(R2_q), .in3(R3_q), .in4(R4_q), .in5(R5_q), .in6(R6_q), .in7(R7_q),
    .out(A_Out), .sel(A_Address));
  Multiplexer #(.select(3), .width(4), .enable("false")) multiplexer_2 (
    .in0(R0_q), .in1(R1_q), .in2(R2_q), .in3(R3_q), .in4(R4_q), .in5(R5_q), .in6(R6_q), .in7(R7_q),
    .out(B__Out), .sel(B_Address));
endmodule

module Function_Unit (
  input  [3:0] B_Out,
  input  [3:0] A_Out,
  input  [3:0] Function_Select,
  output [2:0] PZN,
  output [3:0] F
);

  wire [3:0] adder_1_out, adder_2_out, and_1_out, divider_1_out, multiplier_1_out, not_1_out, or_1_out,
       shifter_1_out, shifter_2_out, shifter_3_out, subtractor_1_out;

  Adder #(.width(4)) adder_1 (.a(not_1_out), .b(4'b0001), .out(adder_1_out));  // open: cin, cout
  assign or_1_out = A_Out | B_Out;  // OR_Gate or_1, 4 bits wide
  assign and_1_out = A_Out & B_Out;  // AND_Gate and_1, 4 bits wide
  assign not_1_out = ~A_Out;  // NOT_Gate not_1, 4 bits wide
  Divider #(.width(4)) divider_1 (.a(A_Out), .b(B_Out), .out(divider_1_out));  // open: upper, rem
  Multiplier #(.width(4)) multiplier_1 (.a(A_Out), .b(B_Out), .out(multiplier_1_out));  // open: cin, cout
  Subtractor #(.width(4)) subtractor_1 (.a(A_Out), .b(B_Out), .out(subtractor_1_out));  // open: bin, bout
  Adder #(.width(4)) adder_2 (.a(A_Out), .b(B_Out), .out(adder_2_out));  // open: cin, cout
  Multiplexer #(.select(4), .width(4)) multiplexer_1 (
    .in0(4'b0000), .in1(4'b0001), .in2(A_Out), .in3(B_Out), .in4(adder_2_out), .in5(subtractor_1_out),
    .in6(multiplier_1_out), .in7(divider_1_out), .in8(not_1_out), .in9(and_1_out), .in10(or_1_out),
    .in11(adder_1_out), .in12(shifter_1_out), .in13(shifter_2_out), .in14(shifter_3_out), .in15(4'b0000),
    .out(F), .sel(Function_Select));  // open: en
  Shifter #(.width(4), .shift("lr")) shifter_1 (.in(A_Out), .\dist (2'b01), .out(shifter_1_out));
  Shifter #(.width(4)) shifter_2 (.in(A_Out), .\dist (2'b01), .out(shifter_2_out));
  Shifter #(.width(4), .shift("ar")) shifter_3 (.in(A_Out), .\dist (2'b01), .out(shifter_3_out));
  Comparator #(.width(4)) comparator_1 (.a(F), .b(4'b0000), .gt(PZN[2]), .eq(PZN[1]), .lt(PZN[0]));
endmodule

module processor (
  input  [15:0] Control_Word,
  input  [3:0] Const_In,
  input  CLK,
  input  [3:0] Data_In,
  output [3:0] Address_Out,
  output [3:0] Data_Out,
  output [2:0] PZN
);

  main main_1 (
    .Control_Word(Control_Word), .CLK(CLK), .constIn(Const_In), .Address_Out(Address_Out),
    .Data_Out(Data_Out), .PZN(PZN), .Data_In(Data_In));
endmodule

// CAR
module Control_Unit (
  input  [2:0] PZN,
  input  [15:0] INSTRUCTION,
  input  START,
  input  RESET,
  input  CLK,
  output [3:0] CONSTANT,
  output MEMORY_WRITE,
  output [15:0] CONTROL_WORD,
  output READY
);

  wire data_partitioner_1_mode, generate_load_signal_1_load;
  wire [1:0] data_partitioner_1_operand_select;
  wire [2:0] PZN_STORE_q;
  wire [7:0] car_1_ca_7_0, generate_data_signal_1_cal_7_0;
  wire [17:0] rom_1_data;

  Register #(.width(3)) PZN_STORE (.D(PZN), .Q(PZN_STORE_q), .clk(CLK));  // open: en, clr
  GENERATE_DATA_SIGNAL generate_data_signal_1 (
    .INSTRUCTION(INSTRUCTION), .NEXT_ADDRESS(CONTROL_WORD[11:4]), .CAL_7_0(generate_data_signal_1_cal_7_0),
    .READY(READY), .START(START));
  CAR car_1 (
    .LOAD(generate_load_signal_1_load), .CAL_7_0(generate_data_signal_1_cal_7_0), .CLK(CLK), .CLR(RESET),
    .CA_7_0(car_1_ca_7_0));
  GENERATE_READY generate_ready_1 (.CA_7_0(car_1_ca_7_0), .READY(READY));
  GENERATE_LOAD_SIGNAL generate_load_signal_1 (
    .PZN(PZN_STORE_q), .CONDITION_CODE(CONTROL_WORD[14:12]), .START(START), .READY(READY),
    .MODE(data_partitioner_1_mode), .LOAD(generate_load_signal_1_load));
  ROM #(.dataWidth(18)) rom_1 (.addr(car_1_ca_7_0), .data(rom_1_data));  // open: sel
  OPERAND_SELECT operand_select_1 (
    .INSTRUCTION(INSTRUCTION), .Constant(CONSTANT), .OPERAND_SELECT(data_partitioner_1_operand_select));
  DATA_PARTITIONER data_partitioner_1 (
    .MICROINSTRUCTION(rom_1_data), .CONTROL_WORD(CONTROL_WORD), .MW(MEMORY_WRITE),
    .MODE(data_partitioner_1_mode), .OPERAND_SELECT(data_partitioner_1_operand_select));

  // Notes on the sheet:
  //   CONTROL STORE
  //   next address
  //   contents of rom_1 (hex, n*v repeats v):
  //   16*0 1231 11400 27000 13*0 1231 1433 2103 10200 27000 11*0 1231 1433 1635 2103 4105 2443 10200 27000
  //   8*0 1231 1433 1635 2103 4105 2453 10200 27000 8*0 1231 1433 1635 2103 4105 2463 10200 27000 8*0 1231
  //   1433 2103 20c3 10200 27000 10*0 1231 1433 2103 2083 10200 27000 10*0 1231 1433 1635 2103 4105 2493
  //   10200 27000 8*0 1635 4105 4025 22200 27000
  //   condition
  //   microinstruction
endmodule

module CAR (
  input  LOAD,
  input  [7:0] CAL_7_0,
  input  CLK,
  input  CLR,
  output [7:0] CA_7_0
);

  wire not_1_out;

  not not_1 (not_1_out, LOAD);
  Counter CAR (.load(LOAD), .D(CAL_7_0), .count(not_1_out), .Q(CA_7_0), .clk(CLK), .clr(CLR));  // open: carry
endmodule

module GENERATE_READY (
  input  [7:0] CA_7_0,
  output READY
);

  Comparator comparator_1 (.a(CA_7_0), .b({8{1'b0}}), .eq(READY));  // open: gt, lt
endmodule

module DATA_PARTITIONER (
  input  [17:0] MICROINSTRUCTION,
  output [15:0] CONTROL_WORD,
  output [1:0] OPERAND_SELECT,
  output MW,
  output MODE
);

  Multiplexer #(.width(4), .enable("false")) multiplexer_1 (
    .in0(MICROINSTRUCTION[3:0]), .in1(4'b0000), .out(CONTROL_WORD[3:0]), .sel(MICROINSTRUCTION[17]));
  Multiplexer #(.enable("false")) multiplexer_2 (
    .in0(MICROINSTRUCTION[15]), .in1(1'b0), .out(CONTROL_WORD[15]), .sel(MICROINSTRUCTION[17]));
  Multiplexer #(.enable("false")) multiplexer_3 (
    .in0(MICROINSTRUCTION[16]), .in1(1'b0), .out(MW), .sel(MICROINSTRUCTION[17]));

  assign CONTROL_WORD[14:4] = MICROINSTRUCTION[14:4];
  assign MODE = MICROINSTRUCTION[17];
  assign OPERAND_SELECT = MICROINSTRUCTION[10:9];

  // Notes on the sheet:
  //   MODE
  //   MW
endmodule

module OPERAND_SELECT (
  input  [15:0] INSTRUCTION,
  input  [1:0] OPERAND_SELECT,
  output [3:0] Constant
);

  Multiplexer #(.select(2), .width(4), .enable("false")) multiplexer_1 (
    .in0(4'b0000), .in1(INSTRUCTION[11:8]), .in2(INSTRUCTION[7:4]), .in3(INSTRUCTION[3:0]), .out(Constant),
    .sel(OPERAND_SELECT));
  // also tied to GND on the sheet: {INSTRUCTION[12], INSTRUCTION[13], INSTRUCTION[14], INSTRUCTION[15]}

  // Notes on the sheet:
  //   OP C
  //   OP B
  //   OP A
endmodule

module GENERATE_DATA_SIGNAL (
  input  [15:0] INSTRUCTION,
  input  [7:0] NEXT_ADDRESS,
  input  READY,
  input  START,
  output [7:0] CAL_7_0
);

  wire and_1_out;

  and and_1 (and_1_out, READY, START);
  Multiplexer #(.width(8), .enable("false")) multiplexer_1 (
    .in0(NEXT_ADDRESS), .in1({INSTRUCTION[15:12], 4'b0000}), .out(CAL_7_0), .sel(and_1_out));
  // also tied to GND on the sheet: {INSTRUCTION[0], INSTRUCTION[1], INSTRUCTION[2], INSTRUCTION[3], INSTRUCTION[4], INSTRUCTION[5], INSTRUCTION[6], INSTRUCTION[7], INSTRUCTION[8], INSTRUCTION[9], INSTRUCTION[10], INSTRUCTION[11]}
endmodule

module GENERATE_LOAD_SIGNAL (
  input  [2:0] PZN,
  input  [2:0] CONDITION_CODE,
  input  START,
  input  READY,
  input  MODE,
  output LOAD
);

  wire and_1_out, multiplexer_2_out, or_1_out, or_2_out, or_3_out;

  and and_1 (and_1_out, START, READY);
  or or_1 (or_1_out, PZN[0], PZN[1]);
  Multiplexer #(.enable("false")) multiplexer_1 (.in0(and_1_out), .in1(multiplexer_2_out), .out(LOAD), .sel(MODE));
  or or_2 (or_2_out, PZN[2], PZN[0]);
  or or_3 (or_3_out, PZN[2], PZN[1]);
  Multiplexer #(.select(3), .enable("false")) multiplexer_2 (
    .in0(1'b0), .in1(PZN[0]), .in2(PZN[1]), .in3(or_1_out), .in4(PZN[2]), .in5(or_2_out), .in6(or_3_out),
    .in7(1'b1), .out(multiplexer_2_out), .sel(CONDITION_CODE));

  // Notes on the sheet:
  //   Negative
  //   Zero
  //   Positive
endmodule

module microprocessor (
  input  [15:0] INSTRUCTION,
  input  START,
  input  RESET,
  input  CLK
);

  wire control_unit_1_memory_write;
  wire [2:0] processor_1_pzn;
  wire [3:0] control_unit_1_constant, processor_1_address_out, processor_1_data_out, ram_1_data;
  wire [15:0] control_unit_1_control_word;

  Control_Unit control_unit_1 (
    .PZN(processor_1_pzn), .INSTRUCTION(INSTRUCTION), .START(START), .RESET(RESET), .CLK(CLK),
    .CONSTANT(control_unit_1_constant), .MEMORY_WRITE(control_unit_1_memory_write),
    .CONTROL_WORD(control_unit_1_control_word));  // open: READY
  processor processor_1 (
    .Control_Word(control_unit_1_control_word), .Const_In(control_unit_1_constant), .PZN(processor_1_pzn),
    .CLK(CLK), .Address_Out(processor_1_address_out), .Data_Out(processor_1_data_out), .Data_In(ram_1_data));
  RAM #(.addrWidth(4), .dataWidth(4), .bus("separate")) ram_1 (
    .addr(processor_1_address_out), .din(processor_1_data_out), .data(ram_1_data),
    .str(control_unit_1_memory_write), .clk(CLK), .ld(1'b1), .clr(RESET));  // open: sel
endmodule
