// Logisim project CPU.circ as structural Verilog
module MAIN (
  input  [27:0] INSTRUCTION,
  input  START,
  input  RESET,
  input  CLK
);

  wire cpu_1_mem_write, cpu_1_ready;
  wire [7:0] cpu_1_address_out, cpu_1_data_out, ram_1_dout;

  LED IDLE (.in(cpu_1_ready));
  CPU cpu_1 (
    .INSTRUCTION(INSTRUCTION), .START(START), .RESET(RESET), .CLK(CLK), .DATA_IN(ram_1_dout),
    .ADDRESS_OUT(cpu_1_address_out), .DATA_OUT(cpu_1_data_out), .READY(cpu_1_ready),
    .MEM_WRITE(cpu_1_mem_write));
  RAM ram_1 (
    .addr(cpu_1_address_out), .we(cpu_1_mem_write), .oe(1'b1), .clk(CLK), .din(cpu_1_data_out),
    .dout(ram_1_dout));

  // Notes on the sheet:
  //   Instruction Encoding
  //   Bits 23-16: Operand A
  //   Bits 15-8: Operand B
  //   Bits 7-0: Operand C
  //   Bits 27-24: Instruction / Program Select
  //   Currently Running Fibonacci(9)
  //   Values Being Written Into Memory
endmodule

module CONTROL_UNIT (
  input  [2:0] PZN,
  input  [27:0] INSTRUCTION,
  input  START,
  input  RESET,
  input  CLK,
  output [15:0] CONTROL_WORD,
  output [7:0] CONST,
  output MEM_WRITE,
  output READY
);

  wire branch_1_load, instruction_decoder_1_mode, not_1_out;
  wire [1:0] instruction_decoder_1_const_sel;
  wire [2:0] PZN_STORE_q;
  wire [7:0] CAR_q, next_addr_1_cal;
  wire [17:0] CONTROL_STORE_data;

  Register #(.width(3)) PZN_STORE (.D(PZN), .en(1'b1), .clk(CLK), .Q(PZN_STORE_q), .clr(RESET));
  NEXT_ADDR next_addr_1 (
    .ADDRESS(CONTROL_WORD[11:4]), .INSTRUCTION(INSTRUCTION), .READY(READY), .START(START),
    .CAL(next_addr_1_cal));
  Counter CAR (
    .clr(RESET), .load(branch_1_load), .up(1'b1), .count(not_1_out), .clk(CLK), .D(next_addr_1_cal), .Q(CAR_q));  // open: carry
  not not_1 (not_1_out, branch_1_load);
  BRANCH branch_1 (
    .PZN(PZN_STORE_q), .CONDITION(CONTROL_WORD[14:12]), .READY(READY), .MODE(instruction_decoder_1_mode),
    .LOAD(branch_1_load));
  Comparator comparator_1 (.a(CAR_q), .b({8{1'b0}}), .eq(READY));  // open: gt, lt
  ROM #(.dataWidth(18)) CONTROL_STORE (.addr(CAR_q), .data(CONTROL_STORE_data));
  Multiplexer #(.select(2), .width(8)) multiplexer_1 (
    .in0({8{1'b0}}), .in1(INSTRUCTION[23:16]), .in2(INSTRUCTION[15:8]), .in3(INSTRUCTION[7:0]), .out(CONST),
    .sel(instruction_decoder_1_const_sel));
  INSTRUCTION_DECODER instruction_decoder_1 (
    .MICROINSTRUCTION(CONTROL_STORE_data), .CONTROL_WORD(CONTROL_WORD),
    .CONST_SEL(instruction_decoder_1_const_sel), .MEM_WRITE(MEM_WRITE), .MODE(instruction_decoder_1_mode));

  // Notes on the sheet:
  //   Instruction Encoding
  //   Bits 15-8: Operand B
  //   Bits 7-0: Operand C
  //   Bits 27-24: Operation/Program Select
  //   Bits 23-16: Operand A
  //   READY
  //   contents of CONTROL_STORE (hex, n*v repeats v):
  //   16*0 1 10000 1237 22000 13 12200 6257 22000 202b a029 8a49 245 2021 4023 18400 6a57 22000 271a0
  //   BRANCH_ADDRESS
  //   Microinstruction Encoding
  //   Internal / Branching Instructions
  //   Bit 17: Mode
  //   External / Data Unit Instructions
  //   Bit 17: Mode
  //   CONST A
  //   CONST B
  //   CONST C
  //   Bits 16-15: 0-Padding
  //   Bits 14-12: Branch Condition
  //   Bits 11-4: Branch Address
  //   Bits 3-0: 0-Padding
  //   Bit 16: Memory Write
  //   Bits 15-0: Control Word
  //   BRANCH_CONDITION
  //   CONST 0
endmodule

module DATA_UNIT (
  input  CLK,
  input  [15:0] CONTROL_WORD,
  input  CLEAR,
  input  [7:0] CONST_IN,
  input  [7:0] DATA_IN,
  output [7:0] ADDR_OUT,
  output [7:0] DATA_OUT,
  output [2:0] PZN
);

  wire [7:0] alu_1_op, multiplexer_2_out, reg_file_1_b_out;

  Multiplexer #(.width(8)) multiplexer_1 (
    .in0(reg_file_1_b_out), .in1(CONST_IN), .out(DATA_OUT), .sel(CONTROL_WORD[12]));
  Multiplexer #(.width(8)) multiplexer_2 (
    .in0(alu_1_op), .in1(DATA_IN), .out(multiplexer_2_out), .sel(CONTROL_WORD[8]));
  REG_FILE reg_file_1 (
    .D_IN(multiplexer_2_out), .CLK(CLK), .WRITE(CONTROL_WORD[0]), .D_ADDR(CONTROL_WORD[3:1]), .CLEAR(CLEAR),
    .A_ADDR(CONTROL_WORD[15:13]), .B_ADDR(CONTROL_WORD[11:9]), .A_OUT(ADDR_OUT), .B_OUT(reg_file_1_b_out));
  ALU alu_1 (.A(ADDR_OUT), .B(DATA_OUT), .OP_SEL(CONTROL_WORD[7:4]), .OP(alu_1_op));
  Comparator comparator_1 (.a(alu_1_op), .b({8{1'b0}}), .gt(PZN[2]), .eq(PZN[1]), .lt(PZN[0]));

  // Notes on the sheet:
  //   B Mux
  //   Control Word Encoding
  //   Bit 12: B Mux
  //   ALU Mux
  //   Bits 15-13: A Address
  //   Bits 11-9: B Address
  //   Bit 8: ALU Mux
  //   Bits 7-4: Op select
  //   Bits 3-1: D Address
  //   Bit 0: Read/Write
  //   Note:
  //   CONST_IN selects the operands from the initial instruction
  //   When B Mux is selected, B Address is used to select which operand to load
endmodule

module ALU (
  input  [7:0] A,
  input  [7:0] B,
  input  [3:0] OP_SEL,
  output [7:0] OP
);

  wire [7:0] adder_subtractor_1_c, and_1_out, multiplier_1_out, negator_1_out, not_1_out, or_1_out,
       shifter_1_out, shifter_2_out, shifter_3_out;

  Shifter #(.shift("ar")) shifter_1 (.in(A), .\dist (3'b001), .out(shifter_1_out));
  Shifter shifter_2 (.in(A), .\dist (3'b001), .out(shifter_2_out));
  Shifter #(.shift("lr")) shifter_3 (.in(A), .\dist (3'b001), .out(shifter_3_out));
  Negator negator_1 (.in(A), .out(negator_1_out));
  assign or_1_out = A | B;  // OR_Gate or_1, 8 bits wide
  assign and_1_out = A & B;  // AND_Gate and_1, 8 bits wide
  assign not_1_out = ~A;  // NOT_Gate not_1, 8 bits wide
  Multiplier multiplier_1 (.a(A), .b(B), .out(multiplier_1_out));  // open: cin, cout
  ADDER_SUBTRACTOR adder_subtractor_1 (.B(B), .Sel(OP_SEL[0]), .A(A), .C(adder_subtractor_1_c));  // open: Cout
  Multiplexer #(.select(4), .width(8)) multiplexer_1 (
    .in0({8{1'b0}}), .in1(8'h1), .in2(A), .in3(B), .in4(adder_subtractor_1_c), .in5(adder_subtractor_1_c),
    .in6(multiplier_1_out), .in7(not_1_out), .in8(and_1_out), .in9(or_1_out), .in10(negator_1_out),
    .in11(shifter_3_out), .in12(shifter_2_out), .in13(shifter_1_out), .in14({8{1'b0}}), .in15({8{1'b0}}),
    .out(OP), .sel(OP_SEL));

  // Notes on the sheet:
  //   Operation Codes
  //   x0 = 0
  //   x1 = 1
  //   x2 = A
  //   x3 = B
  //   xA = -A
  //   xE = 0
  //   xF = 0
  //   x4 = A + B
  //   x5 = A - B
  //   x6 = A * B
  //   x7 = NOT A
  //   x8 = A AND B
  //   x9 = A OR B
  //   xB = A >> 1
  //   xC = A << 1
  //   xD = A >>> 1
endmodule

module ADDER_SUBTRACTOR (
  input  [7:0] A,
  input  [7:0] B,
  input  Sel,
  output Cout,
  output [7:0] C
);

  wire fadder_1_cout, fadder_2_cout, fadder_3_cout, fadder_4_cout, fadder_5_cout, fadder_6_cout,
       fadder_7_cout, xor_1_out, xor_2_out, xor_3_out, xor_4_out, xor_5_out, xor_6_out, xor_7_out, xor_8_out;

  FADDER fadder_1 (.A(A[0]), .B(xor_1_out), .Cin(Sel), .Sum(C[0]), .Cout(fadder_1_cout));
  xor xor_1 (xor_1_out, B[0], Sel);
  FADDER fadder_2 (.A(A[1]), .B(xor_2_out), .Cin(fadder_1_cout), .Sum(C[1]), .Cout(fadder_2_cout));
  xor xor_2 (xor_2_out, B[1], Sel);
  xor xor_3 (xor_3_out, B[2], Sel);
  FADDER fadder_3 (.A(A[2]), .B(xor_3_out), .Cin(fadder_2_cout), .Sum(C[2]), .Cout(fadder_3_cout));
  FADDER fadder_4 (.A(A[3]), .B(xor_4_out), .Cin(fadder_3_cout), .Sum(C[3]), .Cout(fadder_4_cout));
  xor xor_4 (xor_4_out, B[3], Sel);
  xor xor_5 (xor_5_out, B[4], Sel);
  FADDER fadder_5 (.A(A[4]), .B(xor_5_out), .Cin(fadder_4_cout), .Sum(C[4]), .Cout(fadder_5_cout));
  FADDER fadder_6 (.A(A[5]), .B(xor_6_out), .Cin(fadder_5_cout), .Sum(C[5]), .Cout(fadder_6_cout));
  xor xor_6 (xor_6_out, B[5], Sel);
  FADDER fadder_7 (.A(A[6]), .B(xor_7_out), .Cin(fadder_6_cout), .Sum(C[6]), .Cout(fadder_7_cout));
  xor xor_7 (xor_7_out, B[6], Sel);
  xor xor_8 (xor_8_out, B[7], Sel);
  FADDER fadder_8 (.A(A[7]), .B(xor_8_out), .Cin(fadder_7_cout), .Sum(C[7]), .Cout(Cout));
endmodule

module FADDER (
  input  A,
  input  B,
  input  Cin,
  output Sum,
  output Cout
);

  wire nand_1_out, nand_2_out, xor_1_out;

  xor xor_1 (xor_1_out, A, B);
  nand nand_1 (nand_1_out, xor_1_out, Cin);
  nand nand_2 (nand_2_out, A, B);
  xor xor_2 (Sum, xor_1_out, Cin);
  nand nand_3 (Cout, nand_1_out, nand_2_out);
endmodule

module REG_FILE (
  input  [7:0] D_IN,
  input  CLK,
  input  WRITE,
  input  [2:0] D_ADDR,
  input  CLEAR,
  input  [2:0] A_ADDR,
  input  [2:0] B_ADDR,
  output [7:0] A_OUT,
  output [7:0] B_OUT
);

  wire and_1_out, and_2_out, and_3_out, and_4_out, and_5_out, and_6_out, and_7_out, and_8_out,
       decoder_1_out0, decoder_1_out1, decoder_1_out2, decoder_1_out3, decoder_1_out4, decoder_1_out5,
       decoder_1_out6, decoder_1_out7;
  wire [7:0] R0_q, R1_q, R2_q, R3_q, R4_q, R5_q, R6_q, R7_q;

  Decoder #(.enable("false"), .select(3)) decoder_1 (
    .out0(decoder_1_out0), .out1(decoder_1_out1), .out2(decoder_1_out2), .out3(decoder_1_out3),
    .out4(decoder_1_out4), .out5(decoder_1_out5), .out6(decoder_1_out6), .out7(decoder_1_out7), .sel(D_ADDR));
  and and_1 (and_1_out, decoder_1_out0, WRITE);
  Register R0 (.D(D_IN), .en(and_1_out), .clk(CLK), .Q(R0_q), .clr(CLEAR));
  and and_2 (and_2_out, decoder_1_out1, WRITE);
  Register R1 (.D(D_IN), .en(and_2_out), .clk(CLK), .Q(R1_q), .clr(CLEAR));
  and and_3 (and_3_out, decoder_1_out2, WRITE);
  Register R2 (.D(D_IN), .en(and_3_out), .clk(CLK), .Q(R2_q), .clr(CLEAR));
  and and_4 (and_4_out, decoder_1_out3, WRITE);
  Register R3 (.D(D_IN), .en(and_4_out), .clk(CLK), .Q(R3_q), .clr(CLEAR));
  and and_5 (and_5_out, decoder_1_out4, WRITE);
  Register R4 (.D(D_IN), .en(and_5_out), .clk(CLK), .Q(R4_q), .clr(CLEAR));
  and and_6 (and_6_out, decoder_1_out5, WRITE);
  Register R5 (.D(D_IN), .en(and_6_out), .clk(CLK), .Q(R5_q), .clr(CLEAR));
  and and_7 (and_7_out, decoder_1_out6, WRITE);
  Register R6 (.D(D_IN), .en(and_7_out), .clk(CLK), .Q(R6_q), .clr(CLEAR));
  and and_8 (and_8_out, decoder_1_out7, WRITE);
  Register R7 (.D(D_IN), .en(and_8_out), .clk(CLK), .Q(R7_q), .clr(CLEAR));
  Multiplexer #(.select(3), .width(8)) multiplexer_1 (
    .in0(R0_q), .in1(R1_q), .in2(R2_q), .in3(R3_q), .in4(R4_q), .in5(R5_q), .in6(R6_q), .in7(R7_q),
    .out(A_OUT), .sel(A_ADDR));
  Multiplexer #(.select(3), .width(8)) multiplexer_2 (
    .in0(R0_q), .in1(R1_q), .in2(R2_q), .in3(R3_q), .in4(R4_q), .in5(R5_q), .in6(R6_q), .in7(R7_q),
    .out(B_OUT), .sel(B_ADDR));
endmodule

module NEXT_ADDR (
  input  [7:0] ADDRESS,
  input  [27:0] INSTRUCTION,
  input  READY,
  input  START,
  output [7:0] CAL
);

  wire and_1_out;

  and and_1 (and_1_out, READY, START);
  Multiplexer #(.width(8)) multiplexer_1 (
    .in0(ADDRESS), .in1({INSTRUCTION[27:24], 4'b0000}), .out(CAL), .sel(and_1_out));
endmodule

module INSTRUCTION_DECODER (
  input  [17:0] MICROINSTRUCTION,
  output [15:0] CONTROL_WORD,
  output [1:0] CONST_SEL,
  output MEM_WRITE,
  output MODE
);

  Multiplexer multiplexer_1 (
    .in0(MICROINSTRUCTION[15]), .in1(1'b0), .out(CONTROL_WORD[15]), .sel(MICROINSTRUCTION[17]));
  Multiplexer multiplexer_2 (.in0(MICROINSTRUCTION[16]), .in1(1'b0), .out(MEM_WRITE), .sel(MICROINSTRUCTION[17]));
  Multiplexer #(.width(4)) multiplexer_3 (
    .in0(MICROINSTRUCTION[3:0]), .in1(4'b0000), .out(CONTROL_WORD[3:0]), .sel(MICROINSTRUCTION[17]));

  assign CONST_SEL = MICROINSTRUCTION[10:9];
  assign CONTROL_WORD[14:4] = MICROINSTRUCTION[14:4];
  assign MODE = MICROINSTRUCTION[17];
endmodule

module BRANCH (
  input  [2:0] PZN,
  input  [2:0] CONDITION,
  input  READY,
  input  MODE,
  output LOAD
);

  wire multiplexer_1_out, or_1_out, or_2_out, or_3_out;

  or or_1 (or_1_out, PZN[1], PZN[2]);
  or or_2 (or_2_out, PZN[2], PZN[0]);
  or or_3 (or_3_out, PZN[1], PZN[0]);
  Multiplexer #(.select(3)) multiplexer_1 (
    .in0(1'b0), .in1(PZN[0]), .in2(PZN[1]), .in3(or_3_out), .in4(PZN[2]), .in5(or_2_out), .in6(or_1_out),
    .in7(1'b1), .out(multiplexer_1_out), .sel(CONDITION));
  Multiplexer multiplexer_2 (.in0(READY), .in1(multiplexer_1_out), .out(LOAD), .sel(MODE));

  // Notes on the sheet:
  //   N
  //   Z
  //   P
endmodule

module CPU (
  input  [27:0] INSTRUCTION,
  input  START,
  input  RESET,
  input  CLK,
  input  [7:0] DATA_IN,
  output [7:0] ADDRESS_OUT,
  output [7:0] DATA_OUT,
  output READY,
  output MEM_WRITE
);

  wire [2:0] data_unit_1_pzn;
  wire [7:0] control_unit_1_const;
  wire [15:0] control_unit_1_control_word;

  CONTROL_UNIT control_unit_1 (
    .PZN(data_unit_1_pzn), .INSTRUCTION(INSTRUCTION), .START(START), .RESET(RESET), .CLK(CLK),
    .CONTROL_WORD(control_unit_1_control_word), .CONST(control_unit_1_const), .MEM_WRITE(MEM_WRITE),
    .READY(READY));
  DATA_UNIT data_unit_1 (
    .CLK(CLK), .CONTROL_WORD(control_unit_1_control_word), .CLEAR(RESET), .CONST_IN(control_unit_1_const),
    .DATA_IN(DATA_IN), .ADDR_OUT(ADDRESS_OUT), .DATA_OUT(DATA_OUT), .PZN(data_unit_1_pzn));
endmodule
